# Fritzing sketch EMonitor design (saved by Fritzing 0.9.4)
circuit board: 7.5cm x 9cm
breadboards: 2

parts:
  ESP32 = LuaNode32 / ESP32
  C1 = Electrolytic Capacitor [capacitance=1µF package="100 mil [THT, electrolytic]"]
  R1 = Resistor [tolerance=±5% resistance=220 package=THT]
  LDR = Photocell (LDR) [package=THT]
  BMP180 = Barometric Pressure Sensor - BMP180 Breakout (GY-68)
  OLED_Display = OLED 0.96" 128x64 I2C SSD1306
  DHT11 = KY-015 Temperature & Humidity Sensor Module [package="Breakout board"]

nets:
  N1: ESP32.EN, C1.+
  N2: ESP32.VP, R1.Pin_0, LDR.pin_1
  GND: ESP32.GND, C1.-, R1.Pin_1, BMP180.GND, OLED_Display.GND, DHT11.-
  VCC: ESP32.3V3, LDR.pin_0, BMP180.VCC, OLED_Display.VCC, DHT11.S
  N3: ESP32.D4, DHT11.Vin
  N4: ESP32.D21, BMP180.SDA, OLED_Display.SCA
  N5: ESP32.D22, BMP180.SCL, OLED_Display.SCL

notes:
  EMonitor
  by ANJU CHAMANTHA

custom parts:
  LuaNode32 / ESP32: ESP32 based LuaNode32
  KY-015 Temperature & Humidity Sensor Module: KY-015 temperature and humidity sensor module, provides a low-latency serial interface to measure humidity and temperature.
